// Logisim project 0_0000.circ as structural Verilog: 1 circuit, main circuit main
module main (
  input  [7:0] in_1,
  output [7:0] out_2
);


  assign out_2 = in_1;

  // Notes on the sheet:
  //   A
endmodule
