// Logisim project 10_1010.circ as structural Verilog: 1 circuit, main circuit main
module main (
  input  [7:0] A,
  output out_2,
  output [7:0] out_3
);


  assign out_2 = A[7];
  assign out_3 = {A[6:0], 1'b0};

  // Notes on the sheet:
  //   LSL A
endmodule
