// Logisim project 11_1011.circ as structural Verilog: 1 circuit, main circuit main
module main (
  input  [7:0] A,
  output [7:0] out_2,
  output out_3
);


  assign out_2 = {1'b0, A[7:1]};
  assign out_3 = A[0];

  // Notes on the sheet:
  //   LSR A
endmodule
