// Logisim project 12_1100.circ as structural Verilog: 1 circuit, main circuit main
module main (
  input  [7:0] A,
  output [7:0] out_2
);


  assign out_2 = {A[6:0], 1'b0};

  // Notes on the sheet:
  //   ASL A
endmodule
