// Logisim project 13_1101.circ as structural Verilog: 1 circuit, main circuit main
module main (
  input  [7:0] A,
  output [7:0] out_2
);


  assign out_2 = {{2{A[7]}}, A[6:1]};

  // Notes on the sheet:
  //   ASR A
endmodule
