// Logisim project 14_1110.circ as structural Verilog: 1 circuit, main circuit main
module main (
  input  [7:0] A,
  input  Cin,
  output Cout,
  output [7:0] Out
);


  assign Cout = A[7];
  assign Out = {A[6:0], Cin};

  // Notes on the sheet:
  //   CSL A
endmodule
