// Logisim project 15_1111.circ as structural Verilog: 1 circuit, main circuit main
module main (
  input  Cin,
  input  [7:0] A,
  output [7:0] Out,
  output Cout
);


  assign Cout = A[0];
  assign Out = {Cin, A[7:1]};
endmodule
