// Logisim project 16-bitregister.circ as structural Verilog: 1 circuit, main circuit main
module main (
  input  in_1,
  input  [15:0] in_2,
  input  in_3,
  input  in_4,
  output [15:0] out_5
);

  wire adder_1_cout, adder_1_out, adder_2_cout, adder_2_out, adder_3_cout, adder_3_out, adder_4_cout,
       adder_4_out, adder_5_cout, adder_5_out, adder_6_cout, adder_6_out, adder_7_cout, adder_7_out,
       adder_8_cout, adder_8_out, adder_9_cout, adder_9_out, adder_10_cout, adder_10_out, adder_11_cout,
       adder_11_out, adder_12_cout, adder_12_out, adder_13_cout, adder_13_out, adder_14_cout, adder_14_out,
       adder_15_cout, adder_15_out, adder_16_out, clock_1_out, multiplexer_1_out, multiplexer_2_out,
       multiplexer_3_out, multiplexer_4_out, multiplexer_5_out, multiplexer_6_out, multiplexer_7_out,
       multiplexer_8_out, multiplexer_9_out, multiplexer_10_out, multiplexer_11_out, multiplexer_12_out,
       multiplexer_13_out, multiplexer_14_out, multiplexer_15_out, multiplexer_16_out, not_1_out;

  not not_1 (not_1_out, in_4);
  Adder #(.width(1)) adder_1 (.a(out_5[0]), .b(in_4), .out(adder_1_out), .cin(not_1_out), .cout(adder_1_cout));
  Adder #(.width(1)) adder_2 (.a(out_5[1]), .b(in_4), .out(adder_2_out), .cin(adder_1_cout), .cout(adder_2_cout));
  Adder #(.width(1)) adder_3 (.a(out_5[2]), .b(in_4), .out(adder_3_out), .cin(adder_2_cout), .cout(adder_3_cout));
  Adder #(.width(1)) adder_4 (.a(out_5[3]), .b(in_4), .out(adder_4_out), .cin(adder_3_cout), .cout(adder_4_cout));
  Adder #(.width(1)) adder_5 (.a(out_5[4]), .b(in_4), .out(adder_5_out), .cin(adder_4_cout), .cout(adder_5_cout));
  Adder #(.width(1)) adder_6 (.a(out_5[5]), .b(in_4), .out(adder_6_out), .cin(adder_5_cout), .cout(adder_6_cout));
  Adder #(.width(1)) adder_7 (.a(out_5[6]), .b(in_4), .out(adder_7_out), .cin(adder_6_cout), .cout(adder_7_cout));
  Adder #(.width(1)) adder_8 (.a(out_5[7]), .b(in_4), .out(adder_8_out), .cin(adder_7_cout), .cout(adder_8_cout));
  Adder #(.width(1)) adder_9 (.a(out_5[8]), .b(in_4), .out(adder_9_out), .cin(adder_8_cout), .cout(adder_9_cout));
  Adder #(.width(1)) adder_10 (.a(out_5[9]), .b(in_4), .out(adder_10_out), .cin(adder_9_cout), .cout(adder_10_cout));
  Adder #(.width(1)) adder_11 (.a(out_5[10]), .b(in_4), .out(adder_11_out), .cin(adder_10_cout), .cout(adder_11_cout));
  Adder #(.width(1)) adder_12 (.a(out_5[11]), .b(in_4), .out(adder_12_out), .cin(adder_11_cout), .cout(adder_12_cout));
  Adder #(.width(1)) adder_13 (.a(out_5[12]), .b(in_4), .out(adder_13_out), .cin(adder_12_cout), .cout(adder_13_cout));
  Adder #(.width(1)) adder_14 (.a(out_5[13]), .b(in_4), .out(adder_14_out), .cin(adder_13_cout), .cout(adder_14_cout));
  Adder #(.width(1)) adder_15 (.a(out_5[14]), .b(in_4), .out(adder_15_out), .cin(adder_14_cout), .cout(adder_15_cout));
  Adder #(.width(1)) adder_16 (.a(out_5[15]), .b(in_4), .out(adder_16_out), .cin(adder_15_cout));  // open: cout
  Hex_Digit_Display hex_digit_display_1 (.value(in_2[15:12]));  // open: dp
  Hex_Digit_Display hex_digit_display_2 (.value(in_2[11:8]));  // open: dp
  Hex_Digit_Display hex_digit_display_3 (.value(in_2[3:0]));  // open: dp
  Hex_Digit_Display hex_digit_display_4 (.value(in_2[7:4]));  // open: dp
  Multiplexer #(.select(2), .enable("false")) multiplexer_1 (
    .in0(1'b0), .in1(in_2[0]), .in2(adder_1_out), .in3(adder_1_out), .out(multiplexer_1_out),
    .sel({in_3, in_4}));
  Multiplexer #(.select(2), .enable("false")) multiplexer_2 (
    .in0(1'b0), .in1(in_2[1]), .in2(adder_2_out), .in3(adder_2_out), .out(multiplexer_2_out),
    .sel({in_3, in_4}));
  Multiplexer #(.select(2), .enable("false")) multiplexer_3 (
    .in0(1'b0), .in1(in_2[2]), .in2(adder_3_out), .in3(adder_3_out), .out(multiplexer_3_out),
    .sel({in_3, in_4}));
  Multiplexer #(.select(2), .enable("false")) multiplexer_4 (
    .in0(1'b0), .in1(in_2[3]), .in2(adder_4_out), .in3(adder_4_out), .out(multiplexer_4_out),
    .sel({in_3, in_4}));
  Multiplexer #(.select(2), .enable("false")) multiplexer_5 (
    .in0(1'b0), .in1(in_2[4]), .in2(adder_5_out), .in3(adder_5_out), .out(multiplexer_5_out),
    .sel({in_3, in_4}));
  Multiplexer #(.select(2), .enable("false")) multiplexer_6 (
    .in0(1'b0), .in1(in_2[5]), .in2(adder_6_out), .in3(adder_6_out), .out(multiplexer_6_out),
    .sel({in_3, in_4}));
  Multiplexer #(.select(2), .enable("false")) multiplexer_7 (
    .in0(1'b0), .in1(in_2[6]), .in2(adder_7_out), .in3(adder_7_out), .out(multiplexer_7_out),
    .sel({in_3, in_4}));
  Multiplexer #(.select(2), .enable("false")) multiplexer_8 (
    .in0(1'b0), .in1(in_2[7]), .in2(adder_8_out), .in3(adder_8_out), .out(multiplexer_8_out),
    .sel({in_3, in_4}));
  Multiplexer #(.select(2), .enable("false")) multiplexer_9 (
    .in0(1'b0), .in1(in_2[8]), .in2(adder_9_out), .in3(adder_9_out), .out(multiplexer_9_out),
    .sel({in_3, in_4}));
  Multiplexer #(.select(2), .enable("false")) multiplexer_10 (
    .in0(1'b0), .in1(in_2[9]), .in2(adder_10_out), .in3(adder_10_out), .out(multiplexer_10_out),
    .sel({in_3, in_4}));
  Multiplexer #(.select(2), .enable("false")) multiplexer_11 (
    .in0(1'b0), .in1(in_2[10]), .in2(adder_11_out), .in3(adder_11_out), .out(multiplexer_11_out),
    .sel({in_3, in_4}));
  Multiplexer #(.select(2), .enable("false")) multiplexer_12 (
    .in0(1'b0), .in1(in_2[11]), .in2(adder_12_out), .in3(adder_12_out), .out(multiplexer_12_out),
    .sel({in_3, in_4}));
  Multiplexer #(.select(2), .enable("false")) multiplexer_13 (
    .in0(1'b0), .in1(in_2[12]), .in2(adder_13_out), .in3(adder_13_out), .out(multiplexer_13_out),
    .sel({in_3, in_4}));
  Multiplexer #(.select(2), .enable("false")) multiplexer_14 (
    .in0(1'b0), .in1(in_2[13]), .in2(adder_14_out), .in3(adder_14_out), .out(multiplexer_14_out),
    .sel({in_3, in_4}));
  Multiplexer #(.select(2), .enable("false")) multiplexer_15 (
    .in0(1'b0), .in1(in_2[14]), .in2(adder_15_out), .in3(adder_15_out), .out(multiplexer_15_out),
    .sel({in_3, in_4}));
  Multiplexer #(.select(2), .enable("false")) multiplexer_16 (
    .in0(1'b0), .in1(in_2[15]), .in2(adder_16_out), .in3(adder_16_out), .out(multiplexer_16_out),
    .sel({in_3, in_4}));
  Clock clock_1 (.out(clock_1_out));
  D_Flip_Flop d_ff_1 (.clk(clock_1_out), .D(multiplexer_1_out), .Q(out_5[0]), .en(in_1));  // open: Qn, preset, reset
  D_Flip_Flop d_ff_2 (.clk(clock_1_out), .D(multiplexer_2_out), .Q(out_5[1]), .en(in_1));  // open: Qn, preset, reset
  D_Flip_Flop d_ff_3 (.clk(clock_1_out), .D(multiplexer_3_out), .Q(out_5[2]), .en(in_1));  // open: Qn, preset, reset
  D_Flip_Flop d_ff_4 (.clk(clock_1_out), .D(multiplexer_4_out), .Q(out_5[3]), .en(in_1));  // open: Qn, preset, reset
  D_Flip_Flop d_ff_5 (.clk(clock_1_out), .D(multiplexer_5_out), .Q(out_5[4]), .en(in_1));  // open: Qn, preset, reset
  D_Flip_Flop d_ff_6 (.clk(clock_1_out), .D(multiplexer_6_out), .Q(out_5[5]), .en(in_1));  // open: Qn, preset, reset
  D_Flip_Flop d_ff_7 (.clk(clock_1_out), .D(multiplexer_7_out), .Q(out_5[6]), .en(in_1));  // open: Qn, preset, reset
  D_Flip_Flop d_ff_8 (.clk(clock_1_out), .D(multiplexer_8_out), .Q(out_5[7]), .en(in_1));  // open: Qn, preset, reset
  D_Flip_Flop d_ff_9 (.clk(clock_1_out), .D(multiplexer_9_out), .Q(out_5[8]), .en(in_1));  // open: Qn, preset, reset
  D_Flip_Flop d_ff_10 (.clk(clock_1_out), .D(multiplexer_10_out), .Q(out_5[9]), .en(in_1));  // open: Qn, preset, reset
  D_Flip_Flop d_ff_11 (.clk(clock_1_out), .D(multiplexer_11_out), .Q(out_5[10]), .en(in_1));  // open: Qn, preset, reset
  D_Flip_Flop d_ff_12 (.clk(clock_1_out), .D(multiplexer_12_out), .Q(out_5[11]), .en(in_1));  // open: Qn, preset, reset
  D_Flip_Flop d_ff_13 (.clk(clock_1_out), .D(multiplexer_13_out), .Q(out_5[12]), .en(in_1));  // open: Qn, preset, reset
  D_Flip_Flop d_ff_14 (.clk(clock_1_out), .D(multiplexer_14_out), .Q(out_5[13]), .en(in_1));  // open: Qn, preset, reset
  D_Flip_Flop d_ff_15 (.clk(clock_1_out), .D(multiplexer_15_out), .Q(out_5[14]), .en(in_1));  // open: Qn, preset, reset
  D_Flip_Flop d_ff_16 (.clk(clock_1_out), .D(multiplexer_16_out), .Q(out_5[15]), .en(in_1));  // open: Qn, preset, reset
  Hex_Digit_Display hex_digit_display_5 (.value(out_5[15:12]));  // open: dp
  Hex_Digit_Display hex_digit_display_6 (.value(out_5[11:8]));  // open: dp
  Hex_Digit_Display hex_digit_display_7 (.value(out_5[7:4]));  // open: dp
  Hex_Digit_Display hex_digit_display_8 (.value(out_5[3:0]));  // open: dp

  // Notes on the sheet:
  //   FunSel
endmodule
