// Logisim project 2_c.circ as structural Verilog: 1 circuit, main circuit main
module main (
  input  clock,
  input  enable,
  input  [7:0] in_3,
  input  low_high,
  input  in_5,
  input  in_6,
  output [15:0] out_7
);

  wire adder_1_cout, adder_1_out, adder_2_cout, adder_2_out, adder_3_cout, adder_3_out, adder_4_cout,
       adder_4_out, adder_5_cout, adder_5_out, adder_6_cout, adder_6_out, adder_7_cout, adder_7_out,
       adder_8_cout, adder_8_out, adder_9_cout, adder_9_out, adder_10_cout, adder_10_out, adder_11_cout,
       adder_11_out, adder_12_cout, adder_12_out, adder_13_cout, adder_13_out, adder_14_cout, adder_14_out,
       adder_15_cout, adder_15_out, adder_16_out, multiplexer_1_out, multiplexer_2_out, multiplexer_3_out,
       multiplexer_4_out, multiplexer_5_out, multiplexer_6_out, multiplexer_7_out, multiplexer_8_out,
       multiplexer_9_out, multiplexer_10_out, multiplexer_11_out, multiplexer_12_out, multiplexer_13_out,
       multiplexer_14_out, multiplexer_15_out, multiplexer_16_out, not_1_out, not_2_out;
  wire [7:0] demultiplexer_1_out0, demultiplexer_1_out1;

  not not_1 (not_1_out, not_2_out);
  Adder #(.width(1)) adder_1 (.a(out_7[0]), .b(not_2_out), .out(adder_1_out), .cin(not_1_out), .cout(adder_1_cout));
  Adder #(.width(1)) adder_2 (.a(out_7[1]), .b(not_2_out), .out(adder_2_out), .cin(adder_1_cout), .cout(adder_2_cout));
  Adder #(.width(1)) adder_3 (.a(out_7[2]), .b(not_2_out), .out(adder_3_out), .cin(adder_2_cout), .cout(adder_3_cout));
  Adder #(.width(1)) adder_4 (.a(out_7[3]), .b(not_2_out), .out(adder_4_out), .cin(adder_3_cout), .cout(adder_4_cout));
  Adder #(.width(1)) adder_5 (.a(out_7[4]), .b(not_2_out), .out(adder_5_out), .cin(adder_4_cout), .cout(adder_5_cout));
  Adder #(.width(1)) adder_6 (.a(out_7[5]), .b(not_2_out), .out(adder_6_out), .cin(adder_5_cout), .cout(adder_6_cout));
  Adder #(.width(1)) adder_7 (.a(out_7[6]), .b(not_2_out), .out(adder_7_out), .cin(adder_6_cout), .cout(adder_7_cout));
  Adder #(.width(1)) adder_8 (.a(out_7[7]), .b(not_2_out), .out(adder_8_out), .cin(adder_7_cout), .cout(adder_8_cout));
  Adder #(.width(1)) adder_9 (.a(out_7[8]), .b(not_2_out), .out(adder_9_out), .cin(adder_8_cout), .cout(adder_9_cout));
  Adder #(.width(1)) adder_10 (
    .a(out_7[9]), .b(not_2_out), .out(adder_10_out), .cin(adder_9_cout), .cout(adder_10_cout));
  Adder #(.width(1)) adder_11 (
    .a(out_7[10]), .b(not_2_out), .out(adder_11_out), .cin(adder_10_cout), .cout(adder_11_cout));
  Adder #(.width(1)) adder_12 (
    .a(out_7[11]), .b(not_2_out), .out(adder_12_out), .cin(adder_11_cout), .cout(adder_12_cout));
  Adder #(.width(1)) adder_13 (
    .a(out_7[12]), .b(not_2_out), .out(adder_13_out), .cin(adder_12_cout), .cout(adder_13_cout));
  Adder #(.width(1)) adder_14 (
    .a(out_7[13]), .b(not_2_out), .out(adder_14_out), .cin(adder_13_cout), .cout(adder_14_cout));
  Adder #(.width(1)) adder_15 (
    .a(out_7[14]), .b(not_2_out), .out(adder_15_out), .cin(adder_14_cout), .cout(adder_15_cout));
  Adder #(.width(1)) adder_16 (.a(out_7[15]), .b(not_2_out), .out(adder_16_out), .cin(adder_15_cout));  // open: cout
  Demultiplexer #(.width(8), .tristate("true"), .enable("false")) demultiplexer_1 (
    .out0(demultiplexer_1_out0), .out1(demultiplexer_1_out1), .in(in_3), .sel(low_high));
  not not_2 (not_2_out, in_6);
  Hex_Digit_Display hex_digit_display_1 (.value(in_3[7:4]));  // open: dp
  Hex_Digit_Display hex_digit_display_2 (.value(in_3[3:0]));  // open: dp
  Multiplexer #(.select(2), .enable("false")) multiplexer_1 (
    .in0(1'b0), .in1(adder_1_out), .in2(adder_1_out), .in3(demultiplexer_1_out0[0]), .out(multiplexer_1_out),
    .sel({in_5, in_6}));
  Multiplexer #(.select(2), .enable("false")) multiplexer_2 (
    .in0(1'b0), .in1(adder_2_out), .in2(adder_2_out), .in3(demultiplexer_1_out0[1]), .out(multiplexer_2_out),
    .sel({in_5, in_6}));
  Multiplexer #(.select(2), .enable("false")) multiplexer_3 (
    .in0(1'b0), .in1(adder_3_out), .in2(adder_3_out), .in3(demultiplexer_1_out0[2]), .out(multiplexer_3_out),
    .sel({in_5, in_6}));
  Multiplexer #(.select(2), .enable("false")) multiplexer_4 (
    .in0(1'b0), .in1(adder_4_out), .in2(adder_4_out), .in3(demultiplexer_1_out0[3]), .out(multiplexer_4_out),
    .sel({in_5, in_6}));
  Multiplexer #(.select(2), .enable("false")) multiplexer_5 (
    .in0(1'b0), .in1(adder_5_out), .in2(adder_5_out), .in3(demultiplexer_1_out0[4]), .out(multiplexer_5_out),
    .sel({in_5, in_6}));
  Multiplexer #(.select(2), .enable("false")) multiplexer_6 (
    .in0(1'b0), .in1(adder_6_out), .in2(adder_6_out), .in3(demultiplexer_1_out0[5]), .out(multiplexer_6_out),
    .sel({in_5, in_6}));
  Multiplexer #(.select(2), .enable("false")) multiplexer_7 (
    .in0(1'b0), .in1(adder_7_out), .in2(adder_7_out), .in3(demultiplexer_1_out0[6]), .out(multiplexer_7_out),
    .sel({in_5, in_6}));
  Multiplexer #(.select(2), .enable("false")) multiplexer_8 (
    .in0(1'b0), .in2(adder_8_out), .in3(demultiplexer_1_out0[7]), .out(multiplexer_8_out), .sel({in_5, in_6}));  // open: in1
  Multiplexer #(.select(2), .enable("false")) multiplexer_9 (
    .in0(1'b0), .in1(adder_9_out), .in2(adder_9_out), .in3(demultiplexer_1_out1[0]), .out(multiplexer_9_out),
    .sel({in_5, in_6}));
  Multiplexer #(.select(2), .enable("false")) multiplexer_10 (
    .in0(1'b0), .in1(adder_10_out), .in2(adder_10_out), .in3(demultiplexer_1_out1[1]),
    .out(multiplexer_10_out), .sel({in_5, in_6}));
  Multiplexer #(.select(2), .enable("false")) multiplexer_11 (
    .in0(1'b0), .in1(adder_11_out), .in2(adder_11_out), .in3(demultiplexer_1_out1[2]),
    .out(multiplexer_11_out), .sel({in_5, in_6}));
  Multiplexer #(.select(2), .enable("false")) multiplexer_12 (
    .in0(1'b0), .in1(adder_12_out), .in2(adder_12_out), .in3(demultiplexer_1_out1[3]),
    .out(multiplexer_12_out), .sel({in_5, in_6}));
  Multiplexer #(.select(2), .enable("false")) multiplexer_13 (
    .in0(1'b0), .in1(adder_13_out), .in2(adder_13_out), .in3(demultiplexer_1_out1[4]),
    .out(multiplexer_13_out), .sel({in_5, in_6}));
  Multiplexer #(.select(2), .enable("false")) multiplexer_14 (
    .in0(1'b0), .in1(adder_14_out), .in2(adder_14_out), .in3(demultiplexer_1_out1[5]),
    .out(multiplexer_14_out), .sel({in_5, in_6}));
  Multiplexer #(.select(2), .enable("false")) multiplexer_15 (
    .in0(1'b0), .in1(adder_15_out), .in2(adder_15_out), .in3(demultiplexer_1_out1[6]),
    .out(multiplexer_15_out), .sel({in_5, in_6}));
  Multiplexer #(.select(2), .enable("false")) multiplexer_16 (
    .in0(1'b0), .in1(adder_16_out), .in2(adder_16_out), .in3(demultiplexer_1_out1[7]),
    .out(multiplexer_16_out), .sel({in_5, in_6}));
  D_Flip_Flop d_ff_1 (.clk(clock), .D(multiplexer_1_out), .Q(out_7[0]), .en(enable));  // open: Qn, preset, reset
  D_Flip_Flop d_ff_2 (.clk(clock), .D(multiplexer_2_out), .Q(out_7[1]), .en(enable));  // open: Qn, preset, reset
  D_Flip_Flop d_ff_3 (.clk(clock), .D(multiplexer_3_out), .Q(out_7[2]), .en(enable));  // open: Qn, preset, reset
  D_Flip_Flop d_ff_4 (.clk(clock), .D(multiplexer_4_out), .Q(out_7[3]), .en(enable));  // open: Qn, preset, reset
  D_Flip_Flop d_ff_5 (.clk(clock), .D(multiplexer_5_out), .Q(out_7[4]), .en(enable));  // open: Qn, preset, reset
  D_Flip_Flop d_ff_6 (.clk(clock), .D(multiplexer_6_out), .Q(out_7[5]), .en(enable));  // open: Qn, preset, reset
  D_Flip_Flop d_ff_7 (.clk(clock), .D(multiplexer_7_out), .Q(out_7[6]), .en(enable));  // open: Qn, preset, reset
  D_Flip_Flop d_ff_8 (.clk(clock), .D(multiplexer_8_out), .Q(out_7[7]), .en(enable));  // open: Qn, preset, reset
  D_Flip_Flop d_ff_9 (.clk(clock), .D(multiplexer_9_out), .Q(out_7[8]), .en(enable));  // open: Qn, preset, reset
  D_Flip_Flop d_ff_10 (.clk(clock), .D(multiplexer_10_out), .Q(out_7[9]), .en(enable));  // open: Qn, preset, reset
  D_Flip_Flop d_ff_11 (.clk(clock), .D(multiplexer_11_out), .Q(out_7[10]), .en(enable));  // open: Qn, preset, reset
  D_Flip_Flop d_ff_12 (.clk(clock), .D(multiplexer_12_out), .Q(out_7[11]), .en(enable));  // open: Qn, preset, reset
  D_Flip_Flop d_ff_13 (.clk(clock), .D(multiplexer_13_out), .Q(out_7[12]), .en(enable));  // open: Qn, preset, reset
  D_Flip_Flop d_ff_14 (.clk(clock), .D(multiplexer_14_out), .Q(out_7[13]), .en(enable));  // open: Qn, preset, reset
  D_Flip_Flop d_ff_15 (.clk(clock), .D(multiplexer_15_out), .Q(out_7[14]), .en(enable));  // open: Qn, preset, reset
  D_Flip_Flop d_ff_16 (.clk(clock), .D(multiplexer_16_out), .Q(out_7[15]), .en(enable));  // open: Qn, preset, reset
  Hex_Digit_Display hex_digit_display_3 (.value(out_7[11:8]));  // open: dp
  Hex_Digit_Display hex_digit_display_4 (.value(out_7[15:12]));  // open: dp
  Hex_Digit_Display hex_digit_display_5 (.value(out_7[7:4]));  // open: dp
  Hex_Digit_Display hex_digit_display_6 (.value(out_7[3:0]));  // open: dp
endmodule
