// Logisim project 2b.circ as structural Verilog: 1 circuit, main circuit main
module main (
  input  Clock,
  input  [1:0] FunSel,
  input  [7:0] Input,
  input  [1:0] OutCSel,
  input  [1:0] OutDSel,
  input  [2:0] RegSel,
  output [7:0] OutC,
  output [7:0] OutD
);

  wire [7:0] AR_output, PC_output, SP_output;

  Hex_Digit_Display hex_digit_display_1 (.value(Input[7:4]));  // open: dp
  Hex_Digit_Display hex_digit_display_2 (.value(Input[3:0]));  // open: dp
  _8_bit_register_main PC (.FunSel(FunSel), .Input(Input), .Enable(RegSel[0]), .Output(PC_output), .Clock(Clock));
  _8_bit_register_main AR (.FunSel(FunSel), .Input(Input), .Enable(RegSel[1]), .Output(AR_output), .Clock(Clock));
  _8_bit_register_main SP (.FunSel(FunSel), .Input(Input), .Enable(RegSel[2]), .Output(SP_output), .Clock(Clock));
  Multiplexer #(.select(2), .width(8), .enable("false")) multiplexer_1 (
    .in0(PC_output), .in1(AR_output), .in2(SP_output), .in3(PC_output), .out(OutC), .sel(OutCSel));
  Multiplexer #(.select(2), .width(8), .enable("false")) multiplexer_2 (
    .in0(PC_output), .in1(AR_output), .in2(SP_output), .in3(PC_output), .out(OutD), .sel(OutDSel));
  Hex_Digit_Display hex_digit_display_3 (.value(OutC[3:0]));  // open: dp
  Hex_Digit_Display hex_digit_display_4 (.value(OutC[7:4]));  // open: dp
  Hex_Digit_Display hex_digit_display_5 (.value(OutD[7:4]));  // open: dp
  Hex_Digit_Display hex_digit_display_6 (.value(OutD[3:0]));  // open: dp
endmodule
