// Logisim project 4_0100.circ as structural Verilog: 1 circuit, main circuit main
module main (
  input  [7:0] in_1,
  input  [7:0] in_2,
  output Cout,
  output [7:0] Out
);

  Adder adder_1 (.a(in_2), .b(in_1), .out(Out), .cout(Cout));  // open: cin

  // Notes on the sheet:
  //   A
  //   B
endmodule
