// Logisim project 5_0101.circ as structural Verilog: 1 circuit, main circuit main
module main (
  input  Cin,
  input  [7:0] in_2,
  input  [7:0] in_3,
  output Cout,
  output [7:0] Out
);

  Adder adder_1 (.a(in_2), .b(in_3), .out(Out), .cin(Cin), .cout(Cout));

  // Notes on the sheet:
  //   A
  //   B
endmodule
