// Logisim project 6_0110.circ as structural Verilog: 1 circuit, main circuit main
module main (
  input  [7:0] in_1,
  input  [7:0] in_2,
  output Cout,
  output [7:0] Out
);

  wire [7:0] not_1_out;

  assign not_1_out = ~in_2;  // NOT_Gate not_1, 8 bits wide
  Adder adder_1 (.a(in_1), .b(not_1_out), .out(Out), .cin(1'b1), .cout(Cout));

  // Notes on the sheet:
  //   A
  //   B
endmodule
