// Logisim project 8-bit_register.circ as structural Verilog: 1 circuit, main circuit main
module main (
  input  Clock,
  input  [1:0] FunSel,
  input  Enable,
  input  [7:0] Input,
  output [7:0] Output
);

  wire adder_1_cout, adder_1_out, adder_2_cout, adder_2_out, adder_3_cout, adder_3_out, adder_4_cout,
       adder_4_out, adder_5_cout, adder_5_out, adder_6_cout, adder_6_out, adder_7_cout, adder_7_out,
       adder_8_out, multiplexer_1_out, multiplexer_2_out, multiplexer_3_out, multiplexer_4_out,
       multiplexer_5_out, multiplexer_6_out, multiplexer_7_out, multiplexer_8_out, not_1_out, not_2_out;

  not not_1 (not_1_out, FunSel[0]);
  not not_2 (not_2_out, not_1_out);
  Adder #(.width(1)) adder_1 (.a(Output[0]), .b(not_1_out), .out(adder_1_out), .cin(FunSel[0]), .cout(adder_1_cout));
  Adder #(.width(1)) adder_2 (.a(Output[1]), .b(not_2_out), .out(adder_2_out), .cin(adder_1_cout), .cout(adder_2_cout));
  Adder #(.width(1)) adder_3 (.a(Output[2]), .b(not_2_out), .out(adder_3_out), .cin(adder_2_cout), .cout(adder_3_cout));
  Adder #(.width(1)) adder_4 (.a(Output[3]), .b(not_2_out), .out(adder_4_out), .cin(adder_3_cout), .cout(adder_4_cout));
  Adder #(.width(1)) adder_5 (.a(Output[4]), .b(not_2_out), .out(adder_5_out), .cin(adder_4_cout), .cout(adder_5_cout));
  Adder #(.width(1)) adder_6 (.a(Output[5]), .b(not_2_out), .out(adder_6_out), .cin(adder_5_cout), .cout(adder_6_cout));
  Adder #(.width(1)) adder_7 (.a(Output[6]), .b(not_2_out), .out(adder_7_out), .cin(adder_6_cout), .cout(adder_7_cout));
  Adder #(.width(1)) adder_8 (.a(Output[7]), .b(not_2_out), .out(adder_8_out), .cin(adder_7_cout));  // open: cout
  Hex_Digit_Display hex_digit_display_1 (.value(Input[7:4]));  // open: dp
  Multiplexer #(.select(2), .enable("false")) multiplexer_1 (
    .in0(1'b0), .in1(Input[0]), .in2(adder_1_out), .in3(adder_1_out), .out(multiplexer_1_out), .sel(FunSel));
  Multiplexer #(.select(2), .enable("false")) multiplexer_2 (
    .in0(1'b0), .in1(Input[1]), .in2(adder_2_out), .in3(adder_2_out), .out(multiplexer_2_out), .sel(FunSel));
  Multiplexer #(.select(2), .enable("false")) multiplexer_3 (
    .in0(1'b0), .in1(Input[2]), .in2(adder_3_out), .in3(adder_3_out), .out(multiplexer_3_out), .sel(FunSel));
  Multiplexer #(.select(2), .enable("false")) multiplexer_4 (
    .in0(1'b0), .in1(Input[3]), .in2(adder_4_out), .in3(adder_4_out), .out(multiplexer_4_out), .sel(FunSel));
  Multiplexer #(.select(2), .enable("false")) multiplexer_5 (
    .in0(1'b0), .in1(Input[4]), .in2(adder_5_out), .in3(adder_5_out), .out(multiplexer_5_out), .sel(FunSel));
  Multiplexer #(.select(2), .enable("false")) multiplexer_6 (
    .in0(1'b0), .in1(Input[5]), .in2(adder_6_out), .in3(adder_6_out), .out(multiplexer_6_out), .sel(FunSel));
  Multiplexer #(.select(2), .enable("false")) multiplexer_7 (
    .in0(1'b0), .in1(Input[6]), .in2(adder_7_out), .in3(adder_7_out), .out(multiplexer_7_out), .sel(FunSel));
  Multiplexer #(.select(2), .enable("false")) multiplexer_8 (
    .in0(1'b0), .in1(Input[7]), .in2(adder_8_out), .in3(adder_8_out), .out(multiplexer_8_out), .sel(FunSel));
  Hex_Digit_Display hex_digit_display_2 (.value(Input[3:0]));  // open: dp
  D_Flip_Flop d_ff_1 (.clk(Clock), .D(multiplexer_1_out), .Q(Output[0]), .en(Enable));  // open: Qn, preset, reset
  D_Flip_Flop d_ff_2 (.clk(Clock), .D(multiplexer_2_out), .Q(Output[1]), .en(Enable));  // open: Qn, preset, reset
  D_Flip_Flop d_ff_3 (.clk(Clock), .D(multiplexer_3_out), .Q(Output[2]), .en(Enable));  // open: Qn, preset, reset
  D_Flip_Flop d_ff_4 (.clk(Clock), .D(multiplexer_4_out), .Q(Output[3]), .en(Enable));  // open: Qn, preset, reset
  D_Flip_Flop d_ff_5 (.clk(Clock), .D(multiplexer_5_out), .Q(Output[4]), .en(Enable));  // open: Qn, preset, reset
  D_Flip_Flop d_ff_6 (.clk(Clock), .D(multiplexer_6_out), .Q(Output[5]), .en(Enable));  // open: Qn, preset, reset
  D_Flip_Flop d_ff_7 (.clk(Clock), .D(multiplexer_7_out), .Q(Output[6]), .en(Enable));  // open: Qn, preset, reset
  D_Flip_Flop d_ff_8 (.clk(Clock), .D(multiplexer_8_out), .Q(Output[7]), .en(Enable));  // open: Qn, preset, reset
  Hex_Digit_Display hex_digit_display_3 (.value(Output[7:4]));  // open: dp
  Hex_Digit_Display hex_digit_display_4 (.value(Output[3:0]));  // open: dp
endmodule
