// Logisim project 9_1001.circ as structural Verilog: 1 circuit, main circuit main
module main (
  input  [7:0] in_1,
  input  [7:0] in_2,
  output [7:0] Out
);

  assign Out = in_1 ^ in_2;  // XOR_Gate xor_1, 8 bits wide

  // Notes on the sheet:
  //   A
  //   B
endmodule
