// Logisim project ALU.circ as structural Verilog: 1 circuit, main circuit main
module main (
  input  Cin,
  input  [7:0] A,
  input  [7:0] B,
  input  [3:0] FunSel,
  output [7:0] OutAlu,
  output [3:0] ZCNO
);

  wire and_1_out, and_2_out, main_4_cout, main_5_cout, main_8_out_2, main_9_out_3, main_12_cout,
       main_13_cout, main_15_cout, not_1_out, not_2_out, not_3_out, or_1_out, xor_1_out, xor_2_out;
  wire [7:0] main_1_out_2, main_2_out_2, main_3_out_2, main_4_out, main_5_out, main_6_out, main_7_out,
       main_8_out_3, main_9_out_2, main_10_out_2, main_11_out_2, main_12_out, main_13_out, main_14_out_2,
       main_15_out, main_16_out;

  not not_1 (not_1_out, OutAlu[7]);
  and and_1 (and_1_out, A[7], B[7], not_1_out);
  not not_2 (not_2_out, B[7]);
  not not_3 (not_3_out, A[7]);
  and and_2 (and_2_out, not_3_out, not_2_out, OutAlu[7]);
  or or_1 (or_1_out, and_1_out, and_2_out);
  xor xor_1 (xor_1_out, Cin, A[7]);
  _0_0000_main main_1 (.in_1(A), .out_2(main_1_out_2));
  _1_0001_main main_2 (.in_1(B), .out_2(main_2_out_2));
  _2_0010_main main_3 (.in_1(A), .out_2(main_3_out_2));
  _4_0100_main main_4 (.in_1(A), .in_2(B), .Cout(main_4_cout), .Out(main_4_out));
  _6_0110_main main_5 (.in_1(A), .in_2(B), .Cout(main_5_cout), .Out(main_5_out));
  _7_0111_main main_6 (.in_1(A), .in_2(B), .Out(main_6_out));
  _9_1001_main main_7 (.in_1(A), .in_2(B), .Out(main_7_out));
  _10_1010_main main_8 (.A(A), .out_2(main_8_out_2), .out_3(main_8_out_3));
  _11_1011_main main_9 (.A(A), .out_2(main_9_out_2), .out_3(main_9_out_3));
  _12_1100_main main_10 (.A(A), .out_2(main_10_out_2));
  _13_1101_main main_11 (.A(A), .out_2(main_11_out_2));
  _14_1110_main main_12 (.A(A), .Cin(Cin), .Cout(main_12_cout), .Out(main_12_out));
  _15_1111_main main_13 (.Cin(Cin), .A(A), .Out(main_13_out), .Cout(main_13_cout));
  Multiplexer #(.select(4), .enable("false")) multiplexer_1 (
    .in4(or_1_out), .in5(or_1_out), .in6(or_1_out), .in12(xor_2_out), .in14(xor_2_out), .in15(xor_1_out),
    .out(ZCNO[0]), .sel(FunSel));  // open: in0, in1, in2, in3, in7, in8, in9, in10, in11, in13
  _3_0011_main main_14 (.in_1(B), .out_2(main_14_out_2));
  _5_0101_main main_15 (.in_2(A), .in_3(B), .Cin(Cin), .Cout(main_15_cout), .Out(main_15_out));
  _8_1000_main main_16 (.in_1(A), .in_2(B), .Out(main_16_out));
  xor xor_2 (xor_2_out, A[7], A[6]);
  Multiplexer #(.select(4), .enable("false")) multiplexer_2 (
    .in4(main_4_cout), .in5(main_15_cout), .in6(main_5_cout), .in10(main_8_out_2), .in11(main_9_out_3),
    .in14(main_12_cout), .in15(main_13_cout), .out(ZCNO[2]), .sel(FunSel));  // open: in0, in1, in2, in3, in7, in8, in9, in12, in13
  Hex_Digit_Display hex_digit_display_1 (.value(OutAlu[7:4]));  // open: dp
  Multiplexer #(.select(4), .width(8), .enable("false")) multiplexer_3 (
    .in0(main_1_out_2), .in1(main_2_out_2), .in2(main_3_out_2), .in3(main_14_out_2), .in4(main_4_out),
    .in5(main_15_out), .in6(main_5_out), .in7(main_6_out), .in8(main_16_out), .in9(main_7_out),
    .in10(main_8_out_3), .in11(main_9_out_2), .in12(main_10_out_2), .in13(main_11_out_2), .in14(main_12_out),
    .in15(main_13_out), .out(OutAlu), .sel(FunSel));
  Hex_Digit_Display hex_digit_display_2 (.value(OutAlu[3:0]));  // open: dp
  nor nor_1 (ZCNO[3], OutAlu[7], OutAlu[6], OutAlu[5], OutAlu[4], OutAlu[3], OutAlu[2], OutAlu[1], OutAlu[0]);
  Multiplexer #(.select(4), .enable("false")) multiplexer_4 (
    .in0(OutAlu[7]), .in1(OutAlu[7]), .in2(OutAlu[7]), .in3(OutAlu[7]), .in4(OutAlu[7]), .in5(OutAlu[7]),
    .in6(OutAlu[7]), .in7(OutAlu[7]), .in8(OutAlu[7]), .in9(OutAlu[7]), .in10(OutAlu[7]), .in11(OutAlu[7]),
    .in12(OutAlu[7]), .in14(OutAlu[7]), .in15(OutAlu[7]), .out(ZCNO[1]), .sel(FunSel));  // open: in13

  // Notes on the sheet:
  //   4
  //   10
  //   5
  //   6
  //   11
  //   15
  //   14
  //   O
  //   C
  //   Z
  //   N
endmodule
