// Logisim project Final.circ as structural Verilog: 3 circuits, main circuit main
module main (
  output [3:0] OutFlag,
  output [7:0] out_2,
  output [7:0] out_3
);

  wire clk, enable, l_h, muxC, read, write;
  wire [1:0] funsel_AR, funsel_IR, funsel_R, muxA, muxB, outA_R, outB_R, outC_AR, outD_AR;
  wire [2:0] regsel_AR;
  wire [3:0] ALU_zcno, funsel_ALU, main_1_outa, main_1_outa_2, multiplexer_3_out, multiplexer_3_out_2,
       ram_1_data, ram_1_data_2, regsel_R;
  wire [7:0] Adress_Register_File_outc, Adress_Register_File_outd, ALU_outalu, main_1_outb,
       multiplexer_1_out, multiplexer_2_out;

  controller controller_1 (
    .clock(clk), .Z_Flag(OutFlag[3]), .instruction({out_3, out_2}), .enable(enable), .l_h(l_h),
    .\funsel_ır (funsel_IR), .read(read), .regsel_ar(regsel_AR), .funsel_ar(funsel_AR), .outd_ar(outD_AR),
    .muxA(muxA), .regsel_R(regsel_R), .funsel_R(funsel_R), .muxC(muxC), .outA_R(outA_R), .outB_R(outB_R),
    .funsel_ALU(funsel_ALU), .muxB(muxB), .outc_ar(outC_AR), .Write(write));  // open: out_4
  Hex_Digit_Display hex_digit_display_1 (.value(multiplexer_2_out[7:4]));  // open: dp
  Hex_Digit_Display hex_digit_display_2 (.value(multiplexer_2_out[3:0]));  // open: dp
  Hex_Digit_Display hex_digit_display_3 (.value(main_1_outa));  // open: dp
  Hex_Digit_Display hex_digit_display_4 (.value(main_1_outa_2));  // open: dp
  Hex_Digit_Display hex_digit_display_5 (.value(out_2[3:0]));  // open: dp
  Hex_Digit_Display hex_digit_display_6 (.value(out_2[7:4]));  // open: dp
  _8_bit_register_file_2a__main main_1 (
    .FunSel(funsel_R), .Input(multiplexer_2_out), .OutA({main_1_outa_2, main_1_outa}), .OutB(main_1_outb),
    .OutBSel(outB_R), .OutASel(outA_R), .RegSel(regsel_R), .Clock(clk));
  Hex_Digit_Display hex_digit_display_7 (.value(ram_1_data_2));  // open: dp
  Hex_Digit_Display hex_digit_display_8 (.value(main_1_outb[7:4]));  // open: dp
  Hex_Digit_Display hex_digit_display_9 (.value(main_1_outb[3:0]));  // open: dp
  Multiplexer #(.width(8), .enable("false")) multiplexer_1 (
    .in0(Adress_Register_File_outc), .in1({main_1_outa_2, main_1_outa}), .out(multiplexer_1_out), .sel(muxC));
  Multiplexer #(.select(2), .width(8), .enable("false")) multiplexer_2 (
    .in0(out_2), .in1({ram_1_data_2, ram_1_data}), .in2(Adress_Register_File_outc), .in3(ALU_outalu),
    .out(multiplexer_2_out), .sel(muxA));
  Hex_Digit_Display hex_digit_display_10 (.value(ram_1_data));  // open: dp
  _2_c_main _16_Bit_Register (
    .in_3({ram_1_data_2, ram_1_data}), .out_7({out_3, out_2}), .low_high(l_h), .in_5(funsel_IR[1]),
    .in_6(funsel_IR[0]), .enable(enable), .clock(clk));
  Hex_Digit_Display hex_digit_display_11 (.value(out_3[3:0]));  // open: dp
  Hex_Digit_Display hex_digit_display_12 (.value(out_3[7:4]));  // open: dp
  Hex_Digit_Display hex_digit_display_13 (.value(multiplexer_1_out[7:4]));  // open: dp
  Hex_Digit_Display hex_digit_display_14 (.value(multiplexer_3_out_2));  // open: dp
  Multiplexer #(.select(2), .width(8), .enable("false")) multiplexer_3 (
    .in1(out_2), .in2({ram_1_data_2, ram_1_data}), .in3(ALU_outalu),
    .out({multiplexer_3_out_2, multiplexer_3_out}), .sel(muxB));  // open: in0
  Hex_Digit_Display hex_digit_display_15 (.value(multiplexer_1_out[3:0]));  // open: dp
  ALU_main ALU (
    .Cin(OutFlag[2]), .A(multiplexer_1_out), .B(main_1_outb), .FunSel(funsel_ALU), .OutAlu(ALU_outalu),
    .ZCNO(ALU_zcno));
  Hex_Digit_Display hex_digit_display_16 (.value(multiplexer_3_out));  // open: dp
  _2b_main Adress_Register_File (
    .FunSel(funsel_AR), .Input({multiplexer_3_out_2, multiplexer_3_out}), .OutC(Adress_Register_File_outc),
    .OutD(Adress_Register_File_outd), .OutDSel(outD_AR), .OutCSel(outC_AR), .RegSel(regsel_AR), .Clock(clk));
  Clock clock_1 (.out(clk));
  Hex_Digit_Display hex_digit_display_17 (.value(Adress_Register_File_outc[7:4]));  // open: dp
  Hex_Digit_Display hex_digit_display_18 (.value(Adress_Register_File_outd[7:4]));  // open: dp
  Hex_Digit_Display hex_digit_display_19 (.value(Adress_Register_File_outd[3:0]));  // open: dp
  Register #(.width(1)) register_1 (.D(ALU_zcno[0]), .en(1'b1), .Q(OutFlag[0]), .clk(clk), .clr(1'b0));
  Register #(.width(1)) register_2 (.D(ALU_zcno[1]), .en(1'b1), .Q(OutFlag[1]), .clk(clk), .clr(1'b0));
  Register #(.width(1)) register_3 (.D(ALU_zcno[2]), .en(1'b1), .Q(OutFlag[2]), .clk(clk), .clr(1'b0));
  Register #(.width(1)) register_4 (.D(ALU_zcno[3]), .en(1'b1), .Q(OutFlag[3]), .clk(clk), .clr(1'b0));
  Hex_Digit_Display hex_digit_display_20 (.value(Adress_Register_File_outc[3:0]));  // open: dp
  RAM #(.bus("separate")) ram_1 (
    .addr(Adress_Register_File_outd), .din(ALU_outalu), .data({ram_1_data_2, ram_1_data}), .str(write),
    .clk(clk), .ld(read));  // open: sel, clr
  Hex_Digit_Display hex_digit_display_21 (.value(ram_1_data));  // open: dp
  Hex_Digit_Display hex_digit_display_22 (.value(ram_1_data_2));  // open: dp

  // Other names for the same wires on the sheet: Instruction[15:0] = {out_3, out_2}; Z = OutFlag[3]

  // Notes on the sheet:
  //   Register File
  //   Input
  //   OutA
  //   16-bit Regiter
  //   Input
  //   IR (0-7)
  //   OutB
  //   AR
  //   Input
  //   IR(8-15)
  //   A
  //   OutD
  //   OutC
  //   Memory Output
endmodule

module controller (
  input  clock,
  input  Z_Flag,
  input  [15:0] instruction,
  output [2:0] out_4,
  output enable,
  output [1:0] outd_ar,
  output l_h,
  output [1:0] outc_ar,
  output read,
  output [1:0] \funsel_ır ,
  output Write,
  output [2:0] regsel_ar,
  output [1:0] funsel_ar,
  output muxC,
  output [1:0] muxA,
  output [1:0] muxB,
  output [1:0] outA_R,
  output [3:0] regsel_R,
  output [1:0] funsel_R,
  output [3:0] funsel_ALU,
  output [1:0] outB_R
);

  wire and_1_out, and_2_out, and_3_out, and_4_out, and_5_out, and_6_out, and_7_out, and_8_out, and_9_out,
       and_10_out, and_11_out, and_12_out, and_13_out, and_14_out, and_15_out, and_16_out, and_17_out,
       and_18_out, and_19_out, and_20_out, and_21_out, and_22_out, and_23_out, and_24_out, decoder_4_out0,
       decoder_4_out1, F1_1, F1_2, F1_3, F1_4, F1_5, F1_6, F1_7, F1_8, F1_9, F1_10, F1_11, F1_12, F1_13,
       F1_14, F2_1, F2_2, F2_3, F2_4, F2_5, F2_6, F2_7, F2_8, F2_9, F2_10, F2_11, F2_12, F2_13, F2_14,
       input_logic_1_enable, multiplexer_2_out, not_1_out, not_2_out, not_3_out, not_4_out, not_5_out,
       not_6_out, not_7_out, not_8_out, not_9_out, not_10_out, not_11_out, not_12_out, not_13_out,
       not_14_out, not_15_out, not_16_out, not_17_out, not_18_out, not_19_out, not_20_out, or_3_out,
       or_4_out, or_5_out, or_6_out, or_7_out, or_8_out, or_9_out, or_10_out, or_12_out, or_13_out,
       or_15_out, or_16_out, or_17_out, or_18_out, or_19_out, or_20_out, or_21_out, or_22_out, or_23_out,
       or_24_out, or_25_out, or_26_out, or_27_out, or_28_out, S1_AR, S1_PC, S1_R0, S1_R1, S1_R2, S1_R3,
       S1_SP, S2_AR, S2_PC, S2_R0, S2_R1, S2_R2, S2_R3, S2_SP, undriven, xnor_1_out;
  wire [1:0] BR, CD, input_logic_1_s0, OutC_Reg1, OutC_Reg2, OutC_RegDest;
  wire [3:0] Destreg_R, F1, F2, Regsel;
  wire [7:0] AD, adder_1_out, multiplexer_1_out, register_1_q, register_2_q;

  not not_1 (not_1_out, instruction[4]);
  not not_2 (not_2_out, instruction[7]);
  Register register_1 (.D(adder_1_out), .en(input_logic_1_enable), .Q(register_1_q), .clk(clock));  // open: clr
  Multiplexer #(.select(2), .width(8), .enable("false")) multiplexer_1 (
    .in0(adder_1_out), .in1(AD), .in2(register_1_q), .in3({1'b1, instruction[15:11], 2'b00}),
    .out(multiplexer_1_out), .sel(input_logic_1_s0));
  Input_Logic input_logic_1 (
    .T(multiplexer_2_out), .BR1(BR[1]), .BR0(BR[0]), .S1(input_logic_1_s0[1]), .S0(input_logic_1_s0[0]),
    .ENABLE(input_logic_1_enable));
  or or_1 (read, F1_1, F1_2, F1_4, F1_6, F1_8);
  or or_2 (Write, F1_10, F1_5, F1_7);
  and and_1 (and_1_out, F1_12, not_3_out, not_1_out);
  not not_3 (not_3_out, instruction[7]);
  and and_2 (and_2_out, F1_11, not_2_out);
  not not_4 (not_4_out, instruction[10]);
  not not_5 (not_5_out, instruction[7]);
  not not_6 (not_6_out, instruction[4]);
  Multiplexer #(.select(2), .enable("false")) multiplexer_2 (
    .in0(1'b1), .in1(instruction[8]), .in2(Z_Flag), .in3(not_7_out), .out(multiplexer_2_out), .sel(CD));
  not not_7 (not_7_out, Z_Flag);
  and and_3 (and_3_out, F1_13, not_4_out);
  or or_3 (or_3_out, F1_10, F1_5);
  and and_4 (and_4_out, F1_12, not_5_out, instruction[4]);
  and and_5 (and_5_out, F1_12, not_6_out);
  assign outB_R = and_5_out ? instruction[3:2] : 2'bz;  // Controlled_Buffer controlled_buffer_1
  Register register_2 (.D(multiplexer_1_out), .en(1'b1), .Q(register_2_q), .clk(clock));  // open: clr
  or or_4 (or_4_out, and_1_out, and_2_out);
  assign outA_R = or_4_out ? instruction[6:5] : 2'bz;  // Controlled_Buffer controlled_buffer_2
  assign outA_R = and_3_out ? instruction[9:8] : 2'bz;  // Controlled_Buffer controlled_buffer_3
  assign outB_R = or_3_out ? instruction[10:9] : 2'bz;  // Controlled_Buffer controlled_buffer_4
  assign outB_R = and_4_out ? instruction[6:5] : 2'bz;  // Controlled_Buffer controlled_buffer_5
  Adder adder_1 (.a(register_2_q), .b(8'h1), .out(adder_1_out));  // open: cin, cout
  Decoder #(.select(4), .enable("false")) decoder_1 (
    .out1(F1_1), .out2(F1_2), .out3(F1_3), .out4(F1_4), .out5(F1_5), .out6(F1_6), .out7(F1_7), .out8(F1_8),
    .out9(F1_9), .out10(F1_10), .out11(F1_11), .out12(F1_12), .out13(F1_13), .out14(F1_14), .sel(F1));  // open: out0, out15
  Decoder #(.select(4), .enable("false")) decoder_2 (
    .out1(F2_1), .out2(F2_2), .out3(F2_3), .out4(F2_4), .out5(F2_5), .out6(F2_6), .out7(F2_7), .out8(F2_8),
    .out9(F2_9), .out10(F2_10), .out11(F2_11), .out12(F2_12), .out13(F2_13), .out14(F2_14), .sel(F2));  // open: out0, out15
  ROM #(.dataWidth(20)) rom_1 (.addr(register_2_q), .data({F1, F2, CD, BR, AD}), .sel(undriven));
  or or_5 (or_5_out, F1_12, F1_11);
  and and_6 (and_6_out, F2_5, instruction[10]);
  and and_7 (and_7_out, F2_4, instruction[10]);
  or or_6 (or_6_out, F2_4, F1_12, F1_11, F2_5);
  and and_8 (and_8_out, or_5_out, instruction[10]);
  or or_7 (or_7_out, F2_1, F2_3, and_6_out);
  or or_8 (or_8_out, F2_2, and_7_out);
  not not_8 (not_8_out, instruction[10]);
  and and_9 (and_9_out, not_8_out, or_6_out);
  or or_9 (or_9_out, F1_9, F1_8, and_8_out);
  assign funsel_ar = or_9_out ? 2'b01 : 2'bz;  // Controlled_Buffer controlled_buffer_6
  assign funsel_ar = or_7_out ? 2'b10 : 2'bz;  // Controlled_Buffer controlled_buffer_7
  assign funsel_ar = or_8_out ? 2'b11 : 2'bz;  // Controlled_Buffer controlled_buffer_8
  or or_10 (or_10_out, F1_3, F1_4, F1_10, F1_6);
  Decoder #(.select(2), .enable("false")) decoder_3 (
    .out0(Destreg_R[0]), .out1(Destreg_R[1]), .out2(Destreg_R[2]), .out3(Destreg_R[3]), .sel(instruction[9:8]));
  Decoder #(.select(2), .enable("false")) decoder_4 (
    .out0(decoder_4_out0), .out1(decoder_4_out1), .out2(out_4[1]), .out3(out_4[2]), .sel(instruction[9:8]));
  assign regsel_R = or_10_out ? Regsel : 4'bz;  // Controlled_Buffer controlled_buffer_9
  assign regsel_R = and_9_out ? Destreg_R : 4'bz;  // Controlled_Buffer controlled_buffer_10
  Decoder #(.select(2), .enable("false")) decoder_5 (
    .out0(Regsel[0]), .out1(Regsel[1]), .out2(Regsel[2]), .out3(Regsel[3]), .sel(instruction[10:9]));
  or or_11 (out_4[0], decoder_4_out0, decoder_4_out1);
  Decoder #(.select(3), .enable("false")) decoder_6 (
    .out0(S1_R0), .out1(S1_R1), .out2(S1_R2), .out3(S1_R3), .out4(S1_PC), .out5(S1_PC), .out6(S1_AR),
    .out7(S1_SP), .sel(instruction[7:5]));
  or or_12 (or_12_out, F2_2, F1_6, F2_3);
  or or_13 (or_13_out, F2_4, F1_12, F1_11, F2_5);
  and and_10 (and_10_out, or_13_out, instruction[10]);
  or or_14 (enable, F1_1, F1_2);
  or or_15 (or_15_out, F1_8, F2_1, F1_9);
  assign regsel_ar = or_15_out ? 3'b001 : 3'bz;  // Controlled_Buffer controlled_buffer_11
  assign regsel_ar = F1_10 ? 3'b010 : 3'bz;  // Controlled_Buffer controlled_buffer_12
  assign regsel_ar = or_12_out ? 3'b100 : 3'bz;  // Controlled_Buffer controlled_buffer_13
  assign regsel_ar = and_10_out ? out_4 : 3'bz;  // Controlled_Buffer controlled_buffer_14
  not not_9 (not_9_out, instruction[10]);
  or or_16 (or_16_out, F1_12, F1_11);
  and and_11 (and_11_out, not_9_out, or_16_out);
  not not_10 (not_10_out, instruction[10]);
  not not_11 (not_11_out, instruction[10]);
  Decoder #(.select(3), .enable("false")) decoder_7 (
    .out0(S2_R0), .out1(S2_R1), .out2(S2_R2), .out3(S2_R3), .out4(S2_PC), .out5(S2_PC), .out6(S2_AR),
    .out7(S2_SP), .sel(instruction[4:2]));
  or or_17 (or_17_out, F1_1, F1_2);
  or or_18 (or_18_out, F1_3, F1_4, and_11_out, F1_6);
  and and_12 (and_12_out, F2_5, not_10_out);
  assign funsel_R = and_12_out ? 2'b10 : 2'bz;  // Controlled_Buffer controlled_buffer_15
  and and_13 (and_13_out, F2_4, not_11_out);
  assign funsel_R = and_13_out ? 2'b11 : 2'bz;  // Controlled_Buffer controlled_buffer_16
  assign \funsel_ır  = or_17_out ? 2'b11 : 2'bz;  // Controlled_Buffer controlled_buffer_17
  assign funsel_R = or_18_out ? 2'b01 : 2'bz;  // Controlled_Buffer controlled_buffer_18
  assign l_h = F1_1 ? 1'b1 : 1'bz;  // Controlled_Buffer controlled_buffer_19
  assign l_h = F1_2 ? 1'b0 : 1'bz;  // Controlled_Buffer controlled_buffer_20
  not not_12 (not_12_out, instruction[5]);
  not not_13 (not_13_out, instruction[10]);
  or or_19 (or_19_out, F1_12, F1_11);
  not not_14 (not_14_out, instruction[6]);
  and and_14 (and_14_out, instruction[6], not_12_out);
  and and_15 (and_15_out, instruction[6], instruction[5]);
  or or_20 (or_20_out, F1_4, F1_6);
  and and_16 (and_16_out, not_13_out, or_19_out);
  assign OutC_Reg1 = not_14_out ? 2'b00 : 2'bz;  // Controlled_Buffer controlled_buffer_21
  assign OutC_Reg1 = and_14_out ? 2'b01 : 2'bz;  // Controlled_Buffer controlled_buffer_22
  assign OutC_Reg1 = and_15_out ? 2'b10 : 2'bz;  // Controlled_Buffer controlled_buffer_23
  or or_21 (or_21_out, F1_12, F1_11);
  and and_17 (and_17_out, F1_12, instruction[4]);
  assign outc_ar = and_17_out ? OutC_Reg2 : 2'bz;  // Controlled_Buffer controlled_buffer_24
  assign outc_ar = F1_7 ? 2'b00 : 2'bz;  // Controlled_Buffer controlled_buffer_25
  and and_18 (and_18_out, F1_13, instruction[10]);
  assign outc_ar = and_18_out ? OutC_RegDest : 2'bz;  // Controlled_Buffer controlled_buffer_26
  assign muxA = F1_3 ? 2'b00 : 2'bz;  // Controlled_Buffer controlled_buffer_27
  assign muxA = or_20_out ? 2'b01 : 2'bz;  // Controlled_Buffer controlled_buffer_28
  assign muxA = and_16_out ? 2'b11 : 2'bz;  // Controlled_Buffer controlled_buffer_29
  and and_19 (and_19_out, or_21_out, instruction[7]);
  assign outc_ar = and_19_out ? OutC_Reg1 : 2'bz;  // Controlled_Buffer controlled_buffer_30
  or or_22 (or_22_out, F2_11, F1_13, F1_7);
  assign funsel_ALU = F2_6 ? 4'b0110 : 4'bz;  // Controlled_Buffer controlled_buffer_31
  assign funsel_ALU = F2_7 ? 4'b0100 : 4'bz;  // Controlled_Buffer controlled_buffer_32
  assign funsel_ALU = F2_12 ? 4'b0111 : 4'bz;  // Controlled_Buffer controlled_buffer_33
  assign funsel_ALU = F2_13 ? 4'b1000 : 4'bz;  // Controlled_Buffer controlled_buffer_34
  assign funsel_ALU = F2_8 ? 4'b1010 : 4'bz;  // Controlled_Buffer controlled_buffer_35
  assign funsel_ALU = F2_9 ? 4'b1011 : 4'bz;  // Controlled_Buffer controlled_buffer_36
  assign funsel_ALU = F2_10 ? 4'b0010 : 4'bz;  // Controlled_Buffer controlled_buffer_37
  assign funsel_ALU = or_22_out ? 4'b0000 : 4'bz;  // Controlled_Buffer controlled_buffer_38
  or or_23 (or_23_out, F1_10, F1_5);
  assign funsel_ALU = or_23_out ? 4'b0001 : 4'bz;  // Controlled_Buffer controlled_buffer_39
  not not_15 (not_15_out, instruction[3]);
  and and_20 (and_20_out, instruction[3], not_16_out);
  not not_16 (not_16_out, instruction[2]);
  and and_21 (and_21_out, instruction[3], instruction[2]);
  assign OutC_Reg2 = not_15_out ? 2'b00 : 2'bz;  // Controlled_Buffer controlled_buffer_40
  assign OutC_Reg2 = and_20_out ? 2'b01 : 2'bz;  // Controlled_Buffer controlled_buffer_41
  assign OutC_Reg2 = and_21_out ? 2'b10 : 2'bz;  // Controlled_Buffer controlled_buffer_42
  or or_24 (or_24_out, F1_12, F1_11);
  and and_22 (and_22_out, instruction[10], or_24_out);
  or or_25 (or_25_out, F1_10, F1_9);
  assign muxB = or_25_out ? 2'b01 : 2'bz;  // Controlled_Buffer controlled_buffer_43
  assign muxB = F1_5 ? 2'b11 : 2'bz;  // Controlled_Buffer controlled_buffer_44
  assign muxB = F1_8 ? 2'b10 : 2'bz;  // Controlled_Buffer controlled_buffer_45
  assign muxB = and_22_out ? 2'b11 : 2'bz;  // Controlled_Buffer controlled_buffer_46
  not not_17 (not_17_out, instruction[8]);
  or or_26 (or_26_out, F1_1, F1_2);
  or or_27 (or_27_out, F1_4, F1_10);
  not not_18 (not_18_out, instruction[9]);
  assign OutC_RegDest = not_18_out ? 2'b00 : 2'bz;  // Controlled_Buffer controlled_buffer_47
  and and_23 (and_23_out, instruction[9], not_17_out);
  assign OutC_RegDest = and_23_out ? 2'b01 : 2'bz;  // Controlled_Buffer controlled_buffer_48
  and and_24 (and_24_out, instruction[9], instruction[8]);
  assign OutC_RegDest = and_24_out ? 2'b10 : 2'bz;  // Controlled_Buffer controlled_buffer_49
  assign outd_ar = or_26_out ? 2'b00 : 2'bz;  // Controlled_Buffer controlled_buffer_50
  assign outd_ar = or_27_out ? 2'b01 : 2'bz;  // Controlled_Buffer controlled_buffer_51
  or or_28 (or_28_out, F1_5, F1_6, F1_7, F1_8);
  assign outd_ar = or_28_out ? 2'b10 : 2'bz;  // Controlled_Buffer controlled_buffer_52
  xnor xnor_1 (xnor_1_out, instruction[4], instruction[7]);
  assign muxC = F1_12 ? xnor_1_out : 1'bz;  // Controlled_Buffer controlled_buffer_53
  not not_19 (not_19_out, instruction[7]);
  assign muxC = F1_11 ? not_19_out : 1'bz;  // Controlled_Buffer controlled_buffer_54
  assign muxC = F1_7 ? 1'b0 : 1'bz;  // Controlled_Buffer controlled_buffer_55
  not not_20 (not_20_out, instruction[10]);
  assign muxC = F1_13 ? not_20_out : 1'bz;  // Controlled_Buffer controlled_buffer_56

  // Other names for the same wires on the sheet: Adress[7:0] = instruction[7:0]; In0 = instruction[0];
  //   In1 = instruction[1]; In2 = instruction[2]; In3 = instruction[3]; In4 = instruction[4]; In5 = instruction[5];
  //   In6 = instruction[6]; In7 = instruction[7]; clk = clock; Destreg_AR[2:0] = out_4; funsel_IR[1:0] = \funsel_ır ;
  //   AdressMode = instruction[8]; In8 = instruction[8]; In9 = instruction[9]; In10 = instruction[10];
  //   In11 = instruction[11]; In12 = instruction[12]; In13 = instruction[13]; In14 = instruction[14];
  //   In15 = instruction[15]; Z = Z_Flag

  // Notes on the sheet:
  //   MAP
  //   Memory - read
  //   OutA- R
  //   SBR
  //   Memory - write
  //   OutB- R
  //   Input
  //   Incrementer
  //   Enable
  //   contents of rom_1 (hex, n*v repeats v):
  //   11001 21300 126*0 482 30000 40000 0 a0000 0 0 0 bb000 0 0 0 52000 0 0 0 3091 60000 0 0 c7000 0 0 0
  //   c6000 0 0 0 bb09d 409e d0000 0 bb0a1 50a2 d0000 0 cc000 0 0 0 cd000 0 0 0 ba000 0 0 0 b8000 0 0 0
  //   b9000 0 0 0 90000 0 0 0 8b8 0 0 0 cb8 0 0 0 720b8 0 0 0 30c9 80000
  //   IR(15-8)<- M[PC]
  //   IR(7-0)<- M[PC]
  //   Rx<-IR(7-0)
  //   Rx<-M[AR]
  //   M[Sp] <- Rx
  //   Rx <- M[Sp] 
  //   M[sp] <- pc
  //   PC <- M[SP]
  //   PC <- value
  //   Value <- Rx
  //   F2-8,9,10,11
  //   F2-6,7,12,13
  //   for Z-flag
  //   PC<- PC+1
  //   SP <- SP -1
  //   SP <- SP + 1
  //   Dst <-Src1-1
  //   Dst <-Src1+1
  //   Dest<-Src2- Src1
  //   Dest<- Src1+Src2
  //   Dest <- LSL Src1
  //   Dest <- LSR Src1
  //   Dest <- Src1
  //   Dest <- NOT Src1
  //   Dest<- Src1 AND Src2
  //   Dest<- Src1 OR Src2
  //   Microop
  //   Funsel- AR
  //   Regsel- R
  //   Regsel
  //   Destreg
  //   Instruction
  //   Adress mode
  //   0 im 1 dir
  //   Srcreg1
  //   Enable- IR
  //   Regsel- AR
  //   Funsel- R
  //   Adress
  //   Srcreg2
  //   Funsel - IR
  //   L/H - IR
  //   OutC- Reg1
  //   Mux-A
  //   OutC- AR
  //   Funsel-ALU
  //   OutC- Reg2
  //   Mux-B
  //   OutC- RegDest
  //   OutD- AR
  //   Mux-C
endmodule

module Input_Logic (
  input  T,
  input  BR1,
  input  BR0,
  output S1,
  output S0,
  output ENABLE
);

  wire and_1_out, and_2_out, not_1_out, not_2_out;

  not not_1 (not_1_out, BR1);
  not not_2 (not_2_out, BR1);
  and and_1 (and_1_out, BR1, BR0);
  and and_2 (and_2_out, T, not_1_out);
  and and_3 (ENABLE, T, not_2_out, BR0);
  or or_1 (S0, and_1_out, and_2_out);

  assign S1 = BR1;
endmodule
